// Logisim project adders and subractors.circ as structural Verilog: 1 circuit, main circuit main
module main (
  input  in_1,
  input  in_2,
  input  HALF_SUBTRACTOR,
  input  in_4,
  input  FULL_SUBTRACTOR,
  input  in_6,
  input  in_7,
  input  FULL_ADDER,
  input  in_9,
  input  in_10,
  output out_11,
  output out_12,
  output out_13,
  output out_14,
  output out_15,
  output out_16,
  output out_17,
  output out_18
);

  wire and_1_out, and_2_out, and_5_out, and_6_out, and_7_out, and_8_out, not_1_out, not_2_out, not_3_out,
       not_4_out, not_5_out, xor_2_out, xor_3_out;

  not not_1 (not_1_out, in_1);
  not not_2 (not_2_out, HALF_SUBTRACTOR);
  not not_3 (not_3_out, FULL_SUBTRACTOR);
  and and_1 (and_1_out, not_1_out, in_2);
  and and_2 (and_2_out, in_1, not_4_out);
  not not_4 (not_4_out, in_2);
  and and_3 (out_12, in_1, in_2);
  xor xor_1 (out_13, HALF_SUBTRACTOR, in_4);
  and and_4 (out_14, not_2_out, in_4);
  xor xor_2 (xor_2_out, FULL_SUBTRACTOR, in_6);
  xor xor_3 (xor_3_out, FULL_ADDER, in_9);
  and and_5 (and_5_out, FULL_ADDER, in_9);
  not not_5 (not_5_out, xor_2_out);
  xor xor_4 (out_15, xor_2_out, in_7);
  and and_6 (and_6_out, not_5_out, in_7);
  and and_7 (and_7_out, not_3_out, in_6);
  xor xor_5 (out_17, xor_3_out, in_10);
  and and_8 (and_8_out, xor_3_out, in_10);
  or or_1 (out_11, and_1_out, and_2_out);
  or or_2 (out_16, and_6_out, and_7_out);
  or or_3 (out_18, and_8_out, and_5_out);

  // Notes on the sheet:
  //   HALF ADDER
endmodule
